// Logisim project log.circ as structural Verilog
module d_latch (
  input  D,
  input  C,
  output Q
);

  wire and_1_out, and_2_out, nor_1_out, not_1_out;

  not not_1 (not_1_out, D);
  and and_1 (and_1_out, D, C);
  and and_2 (and_2_out, C, not_1_out);
  nor nor_1 (nor_1_out, and_1_out, Q);
  nor nor_2 (Q, nor_1_out, and_2_out);

  // Notes on the sheet:
  //   S
  //   R
  //   S1
  //   R1
endmodule

module d_flipflop (
  input  D,
  input  C,
  output Q
);

  wire d_latch_1_q, not_1_out;

  not not_1 (not_1_out, C);
  d_latch d_latch_1 (.D(D), .C(not_1_out), .Q(d_latch_1_q));
  d_latch d_latch_2 (.D(d_latch_1_q), .C(C), .Q(Q));
endmodule

module Register (
  input  [17:0] in_1,
  input  C,
  output [17:0] out_3
);

  d_flipflop R0 (.D(in_1[0]), .C(C), .Q(out_3[0]));
  d_flipflop R1 (.D(in_1[1]), .C(C), .Q(out_3[1]));
  d_flipflop R2 (.D(in_1[2]), .C(C), .Q(out_3[2]));
  d_flipflop R4 (.D(in_1[4]), .C(C), .Q(out_3[4]));
  d_flipflop R3 (.D(in_1[3]), .C(C), .Q(out_3[3]));
  d_flipflop R5 (.D(in_1[5]), .C(C), .Q(out_3[5]));
  d_flipflop R6 (.D(in_1[6]), .C(C), .Q(out_3[6]));
  d_flipflop R7 (.D(in_1[7]), .C(C), .Q(out_3[7]));
  d_flipflop R8 (.D(in_1[8]), .C(C), .Q(out_3[8]));
  d_flipflop R9 (.D(in_1[9]), .C(C), .Q(out_3[9]));
  d_flipflop R10 (.D(in_1[10]), .C(C), .Q(out_3[10]));
  d_flipflop R12 (.D(in_1[12]), .C(C), .Q(out_3[12]));
  d_flipflop R11 (.D(in_1[11]), .C(C), .Q(out_3[11]));
  d_flipflop R13 (.D(in_1[13]), .C(C), .Q(out_3[13]));
  d_flipflop R14 (.D(in_1[14]), .C(C), .Q(out_3[14]));
  d_flipflop R15 (.D(in_1[15]), .C(C), .Q(out_3[15]));
  d_flipflop R15_2 (.D(in_1[16]), .C(C), .Q(out_3[16]));
  d_flipflop R15_3 (.D(in_1[17]), .C(C), .Q(out_3[17]));
endmodule
